# Fritzing sketch MATTwareHome (saved by Fritzing 0.9.3b)
breadboards: 1

parts:
  D1 = SOLAR-IXYS [package=solarbit-12x1]
  D2 = SOLAR-IXYS [package=solarbit-12x1]
  VCC1 = Battery block 9V
  D3 = Rectifier Diode [part_number=1N4001 package="Melf DO-213 AB [SMD]"]
  VCC2 = Battery block 9V
  Raspberry_Pi_1 = Raspberry Pi 3 [part_number=RPI-3-V1.2]
  LED_Ligh_1 = RELAY [package=relay-jzc]
  LED_Light_2 = RELAY [package=relay-jzc]
  LED_Light_3 = RELAY [package=relay-jzc]
  IR_LED_light_1 = RELAY [package=relay-jzc]
  Q1 = Basic FET N-Channel [package="TO220 [THT]"]
  Q2 = Basic FET N-Channel [package="TO220 [THT]"]
  Q3 = Basic FET N-Channel [package="TO220 [THT]"]
  Q4 = Basic FET N-Channel [package="TO220 [THT]"]
  S1 = Toggle Switch [package=THT]
  U1 = DC-DC_CONVERTER [package=dc-dc_converter]
  5v_power_supply_for_Pi = USB Connectors [package=usb-a-s-silk-female]

nets:
  N1: D1.A, D2.A, VCC1.-, VCC2.-, U1.GND1
  N2: D1.C, D2.C, D3.anode
  N3: VCC1.+, D3.cathode, VCC2.+, S1.COM
  GND: Raspberry_Pi_1.GND, LED_Ligh_1.COIL2, LED_Light_2.COIL2, LED_Light_3.COIL2, IR_LED_light_1.COIL2
  N4: Raspberry_Pi_1.GIPO21, Q1.gate
  N5: Raspberry_Pi_1.GIPO20, Q2.gate
  N6: Raspberry_Pi_1.GIPO16, Q3.gate
  N7: Raspberry_Pi_1.GIPO12, Q4.gate
  5V: Raspberry_Pi_1.5V
  N8: LED_Ligh_1.COIL1, Q1.source
  N9: LED_Light_2.COIL1, Q2.source
  N10: LED_Light_3.COIL1, Q3.source
  N11: IR_LED_light_1.COIL1, Q4.source
  12V: Q1.drain, Q2.drain, Q3.drain, Q4.drain
  N12: S1.L1, U1.VIN
  N13: U1.VOUT, 5v_power_supply_for_Pi.D+
  GND2: U1.GND2, 5v_power_supply_for_Pi.GND
